# Fritzing sketch RFID (saved by Fritzing 0.9.10b)
breadboards: 1

parts:
  Mod1 = Amica NodeMCU DEVKIT 1.0
  Part1 = RFID-RC522-v2
  J1 = Piezo Speaker
  J2 = Basic Servo

nets:
  N1: Mod1.pin1, Mod1.pin_10, Mod1.pin_26, Part1.3.3V
  GND: Mod1.pin2, Mod1.pin_9, Mod1.pin_25, Mod1.pin_29, Part1.GND, J1.pin1, J2.gnd
  N2: Mod1.pin5, Part1.SDA
  N3: Mod1.pin6, Part1.MOSI
  N4: Mod1.pin7, Part1.MISO
  N5: Mod1.pin8, Part1.SCK
  N6: Mod1.pin_11, J2.pulse
  N7: Mod1.pin_14, J1.pin2
  N8: Mod1.pin_15, Part1.RST
  N9: Mod1.pin_30, J2.vcc

notes:
  Rx (ESP-ESP serial)
  Tx (ESP-ESP serial)

custom parts:
  RFID-RC522-v2: A simple China made RFID-RC522 Reader; do check the pin labels, as this is a MFRC522 based clone.
